# Fritzing sketch Simple DC driver for test (saved by Fritzing 0.9.2b)
breadboards: 1

parts:
  VCC1 = 4 x AAA Battery Mount
  M1 = DC Motor
  D1 = Diode [package=diode-1n4148]

nets (from the schematic view):
  GND: VCC1.-, M1.pin_2, D1.C
  N1: VCC1.+, M1.pin_1, D1.A
